# Fritzing sketch schematic (saved by Fritzing 0.9.4)

parts:
  Componente1 = Arduino Nano (Rev3.0) (ICSP)
  LCD2 = LCD screen
  LCM1602_IIC1 = LCM1602 IIC [part_number="LCM1602 IIC" chip_label="LCM1602 IIC" package="DIP (Dual Inline) [THT]"]
  U1 = W5100 mini [package=W5100]
  HLK-PM1 = HLK-PM01
  S1 = Round Pushbutton
  S2 = Round Pushbutton
  S3 = Round Pushbutton
  S4 = Round Pushbutton
  S5 = Round Pushbutton
  S6 = Round Pushbutton
  S7 = Round Pushbutton
  S8 = Round Pushbutton
  S9 = Round Pushbutton

nets:
  N1: Componente1.D2, S8.leg0
  N2: Componente1.D3, S7.leg0
  N3: Componente1.D4, S6.leg0
  N4: Componente1.D5, S5.leg0
  N5: Componente1.D6, S3.leg0
  N6: Componente1.D7, S4.leg0
  N7: Componente1.D8, S2.leg0
  N8: Componente1.D9, S1.leg0
  N9: Componente1.D10, U1.SS
  N10: Componente1.D11/MOSI, U1.MOSI
  N11: Componente1.D12/MISO, U1.MISO
  GND: Componente1.GND, LCM1602_IIC1.GND, U1.GND, HLK-PM1.-Vo, S1.leg1, S2.leg1, S3.leg1, S4.leg1, S5.leg1, S6.leg1, S7.leg1, S8.leg1, S9.leg1
  VCC: Componente1.5V, LCM1602_IIC1.VCC, U1.VCC, HLK-PM1.+Vo
  N12: Componente1.A5, LCM1602_IIC1.SCL
  N13: Componente1.A4, LCM1602_IIC1.SDA
  N14: Componente1.A1, U1.RESET
  N15: Componente1.A0, S9.leg0
  N16: Componente1.D13/SCK, U1.SCK
  VSS: LCD2.VSS, LCM1602_IIC1.VSS
  VDD: LCD2.VDD, LCM1602_IIC1.VDD
  N17: LCD2.V0, LCM1602_IIC1.V0
  N18: LCD2.RS, LCM1602_IIC1.RS
  N19: LCD2.R/W, LCM1602_IIC1.RW
  N20: LCD2.E, LCM1602_IIC1.E
  N21: LCD2.DB0, LCM1602_IIC1.D0
  N22: LCD2.DB1, LCM1602_IIC1.D1
  N23: LCD2.DB2, LCM1602_IIC1.D2
  N24: LCD2.DB3, LCM1602_IIC1.D3
  N25: LCD2.DB4, LCM1602_IIC1.D4
  N26: LCD2.DB5, LCM1602_IIC1.D5
  N27: LCD2.DB6, LCM1602_IIC1.D6
  N28: LCD2.DB7, LCM1602_IIC1.D7
  N29: LCD2.LED+, LCM1602_IIC1.A
  N30: LCD2.LED-, LCM1602_IIC1.K
  N31: LCM1602_IIC1.LED_A, LCM1602_IIC1.LED_B

custom parts:
  LCM1602 IIC: I2C-Module to use a 1602 or 2004 LCD on with the wire.h libory Serial LCD Modul
  W5100 mini: WIZnet W5100 Network Module Mini
